// Digital circuit P19_1.dig as structural Verilog
module P19_1 (
  input  [31:0] instr,
  output [31:0] imm_b,
  output [31:0] imm_j,
  output [31:0] imm_u
);


  assign imm_b = {{20{instr[31]}}, instr[7], instr[30:25], instr[11:8], 1'b0};
  assign imm_j = {{12{instr[31]}}, instr[19:12], instr[20], instr[30:21], 1'b0};
  assign imm_u = {instr[31:12], {12{1'b0}}};

  // Other names for the same wires on the sheet: i7 = instr[7]; i11_8[3:0] = instr[11:8]; i19_12[7:0] = instr[19:12];
  //   i20 = instr[20]; i24_21[3:0] = instr[24:21]; i30_25[5:0] = instr[30:25]; i31 = instr[31]

  // Notes on the sheet:
  //   P19 Immediate generator B/J/U - Digital task
  //   Full size, Splitters only.
  //   Allowed parts: Splitter, Tunnel, Const, Ground, VDD, Text, In, Out, Clock
  //   Do not rename, move or delete the input and output pins.
endmodule

/* Test case public tests:
instr imm_b imm_j imm_u
0x00000000 0x00000000 0x00000000 0x00000000
0xFFFFFFFF 0xFFFFFFFE 0xFFFFFFFE 0xFFFFF000
0x80000000 0xFFFFF000 0xFFF00000 0x80000000
0x00000FFF 0x0000081E 0x00000000 0x00000000
0xFFFFF000 0xFFFFF7E0 0xFFFFFFFE 0xFFFFF000
0x00208063 0x00000000 0x00008002 0x00208000
0xFE000EE3 0xFFFFFFFC 0xFFF007E0 0xFE000000
0x008000EF 0x00000800 0x00000008 0x00800000
0xFFDFF0EF 0xFFFFFFE0 0xFFFFFFFC 0xFFDFF000
0x123450B7 0x00000920 0x00045922 0x12345000
0xFFFFF0B7 0xFFFFFFE0 0xFFFFFFFE 0xFFFFF000
0xAD581E57 0xFFFFF2DC 0xFFF81AD4 0xAD581000
0x0B12AE6E 0x000000BC 0x0002A8B0 0x0B12A000
0xC8EFF346 0xFFFFF486 0xFFFFF48E 0xC8EFF000
0xE539A78B 0xFFFFFE4E 0xFFF9AE52 0xE539A000
0x853D452F 0xFFFFF04A 0xFFFD4852 0x853D4000
0x1EE57012 0x000001E0 0x000571EE 0x1EE57000
0x82F11EC0 0xFFFFF83C 0xFFF1182E 0x82F11000
0x331241A9 0x00000B22 0x00024B30 0x33124000
0x64BEB012 0x00000640 0x000EBE4A 0x64BEB000
0x58E00E8C 0x00000D9C 0x0000058E 0x58E00000
0xFF2F6504 0xFFFFF7EA 0xFFFF67F2 0xFF2F6000
0x877994AF 0xFFFFF868 0xFFF99876 0x87799000
*/
